// Logisim project 2.universalgates.circ as structural Verilog: 1 circuit, main circuit main
module main (
  input  A,
  input  A_2,
  input  B,
  input  B_2,
  input  A_3,
  input  A_4,
  input  B_3,
  input  B_4,
  input  A_5,
  input  A_6,
  output A_B,
  output A_B_2,
  output A_B_3,
  output A_B_4,
  output A_prime,
  output A_prime_2
);

  wire nand_1_out, nand_2_out, nand_3_out, nor_1_out, nor_2_out, nor_3_out;

  nand nand_1 (nand_1_out, A_2, B);
  nand nand_2 (nand_2_out, A_3, A_3);
  nand nand_3 (nand_3_out, B_4, B_4);
  nand nand_4 (A_prime, A_5, A_5);
  nand nand_5 (A_B_2, nand_1_out, nand_1_out);
  nand nand_6 (A_B_3, nand_2_out, nand_3_out);
  nor nor_1 (nor_1_out, A_4, B_3);
  nor nor_2 (nor_2_out, A, A);
  nor nor_3 (nor_3_out, B_2, B_2);
  nor nor_4 (A_prime_2, A_6, A_6);
  nor nor_5 (A_B_4, nor_1_out, nor_1_out);
  nor nor_6 (A_B, nor_2_out, nor_3_out);

  // Notes on the sheet:
  //   AND GATE EQUIVALENT USING NAND
  //   OR GATE EQUIVALENT USING NAND
  //   NOT GATE EQUIVALENT USING NAND
  //   AND GATE EQUIVALENT USING NOR
  //   OR GATE EQUIVALENT USING NOR
  //   NOT GATE EQUIVALENT USING NOR
endmodule
