// Logisim project 3.implementation2.circ as structural Verilog: 1 circuit, main circuit main
module main (
  input  X,
  input  A,
  input  W,
  input  Y,
  input  Z,
  input  X_W_prime_Y_prime_Z_prime,
  input  Y_2,
  input  B,
  input  X_2,
  input  Z_2,
  input  C,
  input  A_2,
  input  A_3,
  input  B_2,
  input  B_3,
  input  C_2,
  output X_prime_Y_Z,
  output AB_BC,
  output AB_prime_A_prime_B,
  output out_20
);

  wire and_1_out, and_2_out, and_3_out, nand_1_out, not_1_out, not_2_out, not_3_out, not_4_out, or_2_out,
       or_3_out, or_5_out;

  not not_1 (not_1_out, X);
  and and_1 (and_1_out, Y_2, Z_2);
  xor xor_1 (AB_prime_A_prime_B, A_2, B_2);
  or or_1 (X_prime_Y_Z, not_1_out, and_1_out);
  not not_2 (not_2_out, A_3);
  not not_3 (not_3_out, B_3);
  not not_4 (not_4_out, B_3);
  and and_2 (and_2_out, A, B);
  and and_3 (and_3_out, B, C);
  or or_2 (or_2_out, not_2_out, not_3_out);
  or or_3 (or_3_out, not_4_out, C_2);
  or or_4 (AB_BC, and_2_out, and_3_out);
  and and_4 (out_20, or_2_out, or_3_out);
  nand nand_1 (nand_1_out, W, Y, Z);
  or or_5 (or_5_out, nand_1_out, X_2);

  // Notes on the sheet:
  //   4. AB'+A"B
  //   1. X' + YZ
  //   X'
  //   Y.Z
  //   IMPLEMENT THE GIVEN BOOLEAN EXPRESSSION USING BASIC GATES
  //   5. (A'+B')(B'+C')
  //   2. AB + BC
  //   A'
  //   B'
  //   B'
  //   AB
  //   BC
  //   A'+B'
  //   B'+C
  //   (A'+B')(B'+C')
  //   3. X+ W' Y' Z'
  //   W'Y'Z'
endmodule
