// Logisim project 4.adder.circ as structural Verilog: 1 circuit, main circuit main
module main (
  input  A,
  input  B,
  input  A_2,
  input  B_2,
  input  C,
  output AB_prime_A_prime_B,
  output AB,
  output Sum,
  output Carry
);

  wire and_2_out, and_3_out, xor_2_out;

  xor xor_1 (AB_prime_A_prime_B, A, B);
  and and_1 (AB, A, B);
  xor xor_2 (xor_2_out, A_2, B_2);
  and and_2 (and_2_out, C, xor_2_out);
  and and_3 (and_3_out, A_2, B_2);
  xor xor_3 (Sum, xor_2_out, C);
  or or_1 (Carry, and_2_out, and_3_out);

  // Notes on the sheet:
  //   HALF ADDER
  //   FULL ADDER
endmodule
