// Logisim project 5.sustractor.circ as structural Verilog: 1 circuit, main circuit main
module main (
  input  A,
  input  B,
  input  A_2,
  input  in_4,
  input  B_2,
  input  C,
  input  in_7,
  input  in_8,
  output DIFF,
  output BORROW,
  output DIFF_2,
  output out_12,
  output BORROW_2
);

  wire and_2_out, and_3_out, and_4_out, not_1_out, not_2_out, xor_3_out;

  xor xor_1 (DIFF, A, B);
  not not_1 (not_1_out, A);
  not not_2 (not_2_out, A_2);
  and and_1 (BORROW, not_1_out, B);
  ExactlyOne xor_2 (.out(DIFF_2), .in0(A_2), .in1(B_2), .in2(C));
  and and_2 (and_2_out, C, not_2_out);
  and and_3 (and_3_out, not_2_out, B_2);
  and and_4 (and_4_out, B_2, C);
  or or_1 (BORROW_2, and_2_out, and_3_out, and_4_out);
  xor xor_3 (xor_3_out, in_4, in_7);
  xor xor_4 (out_12, xor_3_out, in_8);

  // Notes on the sheet:
  //   HALF SUBSTRACTOR
  //   FULL SUBSTRACTOR
endmodule
