// Logisim project 6.multiplexer.circ as structural Verilog: 1 circuit, main circuit main
module main (
  input  Ao,
  input  So,
  input  A1,
  input  AO_2,
  input  So_2,
  input  S1,
  input  A1_2,
  input  A2,
  input  A3,
  input  A0,
  input  So_3,
  input  A1_3,
  input  S1_2,
  input  A2_2,
  input  S2,
  input  A3_2,
  input  A4,
  input  A5,
  input  A6,
  input  A7,
  input  So_4,
  input  Ao_3,
  input  A1_4,
  input  S1_3,
  input  A2_3,
  input  A3_3,
  input  S2_2,
  input  A4_2,
  input  A5_2,
  input  S3,
  input  A6_2,
  input  A7_2,
  input  A8,
  input  A9,
  input  A10,
  input  A11,
  input  A12,
  input  A13,
  input  A14,
  input  A15,
  output Y,
  output Y_2,
  output Y_3,
  output Y_4
);

  wire and_1_out, and_2_out, and_3_out, and_4_out, and_5_out, and_6_out, and_7_out, and_8_out, and_9_out,
       and_10_out, and_11_out, and_12_out, and_13_out, and_14_out, and_15_out, and_16_out, and_17_out,
       and_18_out, and_19_out, and_20_out, and_21_out, and_22_out, and_23_out, and_24_out, and_25_out,
       and_26_out, and_27_out, and_28_out, and_29_out, and_30_out, not_1_out, not_2_out, not_3_out,
       not_4_out, not_5_out, not_6_out, not_7_out, not_8_out, not_9_out, not_10_out;

  not not_1 (not_1_out, So_3);
  not not_2 (not_2_out, S1_2);
  not not_3 (not_3_out, S2);
  not not_4 (not_4_out, So);
  not not_5 (not_5_out, So_2);
  not not_6 (not_6_out, S1);
  not not_7 (not_7_out, So_4);
  not not_8 (not_8_out, S1_3);
  not not_9 (not_9_out, S2_2);
  not not_10 (not_10_out, S3);
  and and_1 (and_1_out, Ao, not_4_out);
  and and_2 (and_2_out, So, A1);
  and and_3 (and_3_out, AO_2, not_5_out, not_6_out);
  and and_4 (and_4_out, not_6_out, So_2, A1_2);
  and and_5 (and_5_out, S1, not_5_out, A2);
  and and_6 (and_6_out, So_2, S1, A3);
  and and_7 (and_7_out, Ao_3, not_7_out, not_8_out, not_9_out, not_10_out);
  and and_8 (and_8_out, A1_4, not_7_out, not_8_out, not_9_out, S3);
  and and_9 (and_9_out, A2_3, S2_2, not_7_out, not_8_out, not_10_out);
  and and_10 (and_10_out, A3_3, not_7_out, not_8_out, S2_2, S3);
  and and_11 (and_11_out, A4_2, not_7_out, S1_3, not_9_out, not_10_out);
  and and_12 (and_12_out, A5_2, not_7_out, S1_3, S3, not_9_out);
  and and_13 (and_13_out, A6_2, not_7_out, S2_2, S1_3, not_10_out);
  and and_14 (and_14_out, A7_2, not_7_out, S1_3, S2_2, S3);
  and and_15 (and_15_out, A8, not_8_out, not_9_out, not_10_out, So_4);
  and and_16 (and_16_out, A9, not_8_out, not_9_out, S3, So_4);
  and and_17 (and_17_out, A10, not_8_out, S2_2, not_10_out, So_4);
  and and_18 (and_18_out, A11, not_8_out, S2_2, S3, So_4);
  and and_19 (and_19_out, A12, S1_3, not_9_out, not_10_out, So_4);
  and and_20 (and_20_out, A13, not_9_out, S3, S1_3, So_4);
  and and_21 (and_21_out, A14, not_10_out, S2_2, S1_3, So_4);
  and and_22 (and_22_out, A15, S3, S2_2, S1_3, So_4);
  or or_1 (Y, and_1_out, and_2_out);
  or or_2 (Y_2, and_3_out, and_4_out, and_5_out, and_6_out);
  and and_23 (and_23_out, A0, not_1_out, not_2_out, not_3_out);
  and and_24 (and_24_out, A1_3, not_1_out, not_2_out, S2);
  and and_25 (and_25_out, A2_2, not_1_out, S1_2, not_3_out);
  and and_26 (and_26_out, A3_2, not_1_out, S1_2, S2);
  and and_27 (and_27_out, A4, So_3, not_2_out, not_3_out);
  and and_28 (and_28_out, A5, So_3, not_2_out, S2);
  and and_29 (and_29_out, A6, So_3, S1_2, not_3_out);
  and and_30 (and_30_out, A7, S2, S1_2, So_3);
  or or_3 (Y_4, and_7_out, and_8_out, and_9_out, and_10_out, and_11_out, and_12_out, and_13_out, and_14_out, and_15_out, and_16_out, and_17_out, and_18_out, and_19_out, and_20_out, and_21_out, and_22_out);
  or or_4 (Y_3, and_23_out, and_24_out, and_25_out, and_26_out, and_27_out, and_28_out, and_29_out, and_30_out);

  // Notes on the sheet:
  //   MULTIPLEXER
  //   2:1 MULTIPLEXER
  //   4:1 MULTIPLEXER
  //   8:1 MULTIPLEXER
  //   16:1 MULTIPLEXER
endmodule
