// Logisim project 7.decoder.circ as structural Verilog: 1 circuit, main circuit main
module main (
  input  A,
  input  B,
  input  A_2,
  input  B_2,
  input  C,
  input  A_3,
  input  B_3,
  input  C_2,
  input  D,
  output Do,
  output D1,
  output D2,
  output D3,
  output Do_2,
  output D1_2,
  output D2_2,
  output D3_2,
  output D4,
  output D5,
  output D6,
  output D7,
  output Do_3,
  output D1_3,
  output D2_3,
  output D3_3,
  output D4_2,
  output D5_2,
  output D6_2,
  output D7_2,
  output D8,
  output D9,
  output D10,
  output D11,
  output D12,
  output D13,
  output D14,
  output D15
);

  wire not_1_out, not_2_out, not_3_out, not_4_out, not_5_out, not_6_out, not_7_out, not_8_out, not_9_out;

  not not_1 (not_1_out, A_2);
  not not_2 (not_2_out, B_2);
  not not_3 (not_3_out, C);
  not not_4 (not_4_out, A);
  not not_5 (not_5_out, B);
  not not_6 (not_6_out, A_3);
  not not_7 (not_7_out, B_3);
  not not_8 (not_8_out, C_2);
  not not_9 (not_9_out, D);
  and and_1 (Do, not_4_out, not_5_out);
  and and_2 (D1, not_4_out, B);
  and and_3 (D2, not_5_out, A);
  and and_4 (D3, B, A);
  and and_5 (Do_2, not_1_out, not_2_out, not_3_out);
  and and_6 (D1_2, not_1_out, not_2_out, C);
  and and_7 (D2_2, not_1_out, not_3_out, B_2);
  and and_8 (D3_2, not_1_out, B_2, C);
  and and_9 (D4, A_2, not_2_out, not_3_out);
  and and_10 (D5, not_2_out, C, A_2);
  and and_11 (D6, not_3_out, B_2, A_2);
  and and_12 (D7, B_2, C, A_2);
  and and_13 (Do_3, not_6_out, not_7_out, not_8_out, not_9_out);
  and and_14 (D1_3, not_6_out, not_7_out, not_8_out, D);
  and and_15 (D2_3, not_6_out, not_7_out, not_9_out, C_2);
  and and_16 (D3_3, not_6_out, not_7_out, D, C_2);
  and and_17 (D4_2, not_6_out, not_9_out, not_8_out, B_3);
  and and_18 (D5_2, B_3, D, not_6_out, not_8_out);
  and and_19 (D6_2, B_3, C_2, not_6_out, not_9_out);
  and and_20 (D7_2, B_3, C_2, D, not_6_out);
  and and_21 (D8, A_3, not_8_out, not_7_out, not_9_out);
  and and_22 (D9, not_7_out, not_8_out, D, A_3);
  and and_23 (D10, not_7_out, not_9_out, C_2, A_3);
  and and_24 (D11, D, not_7_out, C_2, A_3);
  and and_25 (D12, not_8_out, not_9_out, B_3, A_3);
  and and_26 (D13, not_8_out, D, B_3, A_3);
  and and_27 (D14, not_9_out, C_2, B_3, A_3);
  and and_28 (D15, D, C_2, B_3, A_3);

  // Notes on the sheet:
  //   DECODERS
  //   2:4 DECODER
  //   3:8 DECODER
  //   4:16 DECODER
endmodule
