// Logisim project 8-bit_ALU_Direct_Addressing_Mode_Basic.circ as structural Verilog: 3 circuits, main circuit main
module main (
  input  [7:0] in_1,
  input  [7:0] Data_in,
  input  R_W_prime,
  input  [7:0] Data,
  output [15:0] out_5
);

  wire clock_1_out, not_1_out;
  wire [7:0] ram_1_data, Reg_File_data_out__8_bits, rom_1_data;
  wire [14:8] rom_1_data_2;

  ROM #(.dataWidth(15)) rom_1 (.addr(in_1), .data({rom_1_data_2, rom_1_data}));  // open: sel
  Clock clock_1 (.out(clock_1_out));
  not not_1 (not_1_out, R_W_prime);
  Reg_File Reg_File (
    .Data_in__8_bits(Data_in), .Rx__3_bits(rom_1_data_2[10:8]), .Clock(clock_1_out), .R_W_prime(R_W_prime),
    .Data_out__8_bits(Reg_File_data_out__8_bits));
  RAM #(.bus("separate")) ram_1 (
    .addr(rom_1_data), .din(Data), .data(ram_1_data), .str(not_1_out), .clk(clock_1_out), .ld(R_W_prime));  // open: sel, clr
  Hex_Digit_Display hex_digit_display_1 (.value(Reg_File_data_out__8_bits[3:0]));  // open: dp
  Hex_Digit_Display hex_digit_display_2 (.value(Reg_File_data_out__8_bits[7:4]));  // open: dp
  Hex_Digit_Display hex_digit_display_3 (.value(ram_1_data[7:4]));  // open: dp
  Hex_Digit_Display hex_digit_display_4 (.value(out_5[15:12]));  // open: dp
  ALU_8_Bit ALU (.A(Reg_File_data_out__8_bits), .B(ram_1_data), .Opcode(rom_1_data_2[14:11]), .Output(out_5));
  Hex_Digit_Display hex_digit_display_5 (.value(ram_1_data[3:0]));  // open: dp
  Hex_Digit_Display hex_digit_display_6 (.value(out_5[7:4]));  // open: dp
  Hex_Digit_Display hex_digit_display_7 (.value(out_5[11:8]));  // open: dp
  Hex_Digit_Display hex_digit_display_8 (.value(out_5[3:0]));  // open: dp

  // Notes on the sheet:
  //   code memory/RoM
  //   contents of rom_1 (hex, n*v repeats v):
  //   202
  //   ADD R2, 0x02
  //   SUB R1, 0x01
  //   XOR R3, 0x03
  //   SHL R4,0x00
endmodule

module Reg_File (
  input  [7:0] Data_in__8_bits,
  input  [2:0] Rx__3_bits,
  input  Clock,
  input  R_W_prime,
  output [7:0] Data_out__8_bits
);

  wire decoder_1_out0, decoder_1_out1, decoder_1_out2, decoder_1_out3, decoder_1_out4, decoder_1_out5,
       decoder_1_out6, decoder_1_out7, not_1_out;
  wire [7:0] R0_q, R1_q, R2_q, R3_q, R4_q, R5_q, R6_q, R7_q;

  Hex_Digit_Display hex_digit_display_1 (.value(Data_in__8_bits[3:0]));  // open: dp
  Hex_Digit_Display hex_digit_display_2 (.value(Data_in__8_bits[7:4]));  // open: dp
  Decoder #(.select(3), .disabled(0)) decoder_1 (
    .out0(decoder_1_out0), .out1(decoder_1_out1), .out2(decoder_1_out2), .out3(decoder_1_out3),
    .out4(decoder_1_out4), .out5(decoder_1_out5), .out6(decoder_1_out6), .out7(decoder_1_out7),
    .sel(Rx__3_bits), .en(not_1_out));
  not not_1 (not_1_out, R_W_prime);
  Register R0 (.D(Data_in__8_bits), .en(decoder_1_out0), .Q(R0_q), .clk(Clock));  // open: clr
  Register R1 (.D(Data_in__8_bits), .en(decoder_1_out1), .Q(R1_q), .clk(Clock));  // open: clr
  Register R2 (.D(Data_in__8_bits), .en(decoder_1_out2), .Q(R2_q), .clk(Clock));  // open: clr
  Register R3 (.D(Data_in__8_bits), .en(decoder_1_out3), .Q(R3_q), .clk(Clock));  // open: clr
  Register R4 (.D(Data_in__8_bits), .en(decoder_1_out4), .Q(R4_q), .clk(Clock));  // open: clr
  Register R5 (.D(Data_in__8_bits), .en(decoder_1_out5), .Q(R5_q), .clk(Clock));  // open: clr
  Register R6 (.D(Data_in__8_bits), .en(decoder_1_out6), .Q(R6_q), .clk(Clock));  // open: clr
  Register R7 (.D(Data_in__8_bits), .en(decoder_1_out7), .Q(R7_q), .clk(Clock));  // open: clr
  Hex_Digit_Display hex_digit_display_3 (.value(Data_out__8_bits[7:4]));  // open: dp
  Hex_Digit_Display hex_digit_display_4 (.value(Data_out__8_bits[3:0]));  // open: dp
  Multiplexer #(.select(3), .width(8)) multiplexer_1 (
    .in0(R0_q), .in1(R1_q), .in2(R2_q), .in3(R3_q), .in4(R4_q), .in5(R5_q), .in6(R6_q), .in7(R7_q),
    .out(Data_out__8_bits), .sel(Rx__3_bits), .en(R_W_prime));

  // Notes on the sheet:
  //   8-bit Register File (R0-R7)
endmodule

module ALU_8_Bit (
  input  [7:0] A,
  input  [7:0] B,
  input  [3:0] Opcode,
  output [15:0] Output
);

  wire adder_1_cout, comparator_1_eq, comparator_1_gt, comparator_1_lt, subtractor_1_bout;
  wire [2:0] bit_extender_1_out;
  wire [3:0] bit_extender_12_out, bit_extender_13_out;
  wire [7:0] adder_1_out, and_1_out, bit_extender_2_out, bit_extender_3_out, bit_extender_14_out,
       divider_1_out, divider_1_rem, multiplier_1_cout, multiplier_1_out, nand_1_out, or_1_out,
       shifter_1_out, shifter_2_out, shifter_3_out, shifter_4_out, subtractor_1_out, xor_1_out;
  wire [15:0] bit_extender_4_out, bit_extender_5_out, bit_extender_6_out, bit_extender_7_out,
       bit_extender_8_out, bit_extender_9_out, bit_extender_10_out, bit_extender_11_out;

  Hex_Digit_Display hex_digit_display_1 (.value(A[7:4]));  // open: dp
  Hex_Digit_Display hex_digit_display_2 (.value(A[3:0]));  // open: dp
  Hex_Digit_Display hex_digit_display_3 (.value(B[3:0]));  // open: dp
  Hex_Digit_Display hex_digit_display_4 (.value(B[7:4]));  // open: dp
  Adder adder_1 (.a(A), .b(B), .out(adder_1_out), .cout(adder_1_cout));  // open: cin
  Subtractor subtractor_1 (.a(A), .b(B), .out(subtractor_1_out), .bout(subtractor_1_bout));  // open: bin
  Multiplier multiplier_1 (.a(A), .b(B), .out(multiplier_1_out), .cout(multiplier_1_cout));  // open: cin
  Divider divider_1 (.a(A), .b(B), .out(divider_1_out), .rem(divider_1_rem));  // open: upper
  assign and_1_out = A & B;  // AND_Gate and_1, 8 bits wide
  assign or_1_out = A | B;  // OR_Gate or_1, 8 bits wide
  assign nand_1_out = ~(A & B);  // NAND_Gate nand_1, 8 bits wide
  assign xor_1_out = A ^ B;  // XOR_Gate xor_1, 8 bits wide
  Bit_Extender #(.out_width(3)) bit_extender_1 (.in(B), .out(bit_extender_1_out));
  assign bit_extender_2_out = {{7{1'b0}}, adder_1_cout};  // Bit_Extender bit_extender_2
  assign bit_extender_3_out = {{7{1'b0}}, subtractor_1_bout};  // Bit_Extender bit_extender_3
  assign bit_extender_4_out = {{8{1'b0}}, and_1_out};  // Bit_Extender bit_extender_4
  assign bit_extender_5_out = {{8{1'b0}}, or_1_out};  // Bit_Extender bit_extender_5
  assign bit_extender_6_out = {{8{1'b0}}, nand_1_out};  // Bit_Extender bit_extender_6
  assign bit_extender_7_out = {{8{1'b0}}, xor_1_out};  // Bit_Extender bit_extender_7
  Shifter shifter_1 (.in(A), .\dist (bit_extender_1_out), .out(shifter_1_out));
  Shifter #(.shift("lr")) shifter_2 (.in(A), .\dist (bit_extender_1_out), .out(shifter_2_out));
  Shifter #(.shift("rl")) shifter_3 (.in(A), .\dist (bit_extender_1_out), .out(shifter_3_out));
  Shifter #(.shift("rr")) shifter_4 (.in(A), .\dist (bit_extender_1_out), .out(shifter_4_out));
  assign bit_extender_8_out = {{8{1'b0}}, shifter_1_out};  // Bit_Extender bit_extender_8
  assign bit_extender_9_out = {{8{1'b0}}, shifter_2_out};  // Bit_Extender bit_extender_9
  assign bit_extender_10_out = {{8{1'b0}}, shifter_3_out};  // Bit_Extender bit_extender_10
  assign bit_extender_11_out = {{8{1'b0}}, shifter_4_out};  // Bit_Extender bit_extender_11
  Comparator comparator_1 (.a(A), .b(B), .gt(comparator_1_gt), .eq(comparator_1_eq), .lt(comparator_1_lt));
  assign bit_extender_12_out = {{3{1'b0}}, comparator_1_gt};  // Bit_Extender bit_extender_12
  assign bit_extender_13_out = {{3{1'b0}}, comparator_1_eq};  // Bit_Extender bit_extender_13
  assign bit_extender_14_out = {{7{1'b0}}, comparator_1_lt};  // Bit_Extender bit_extender_14
  Hex_Digit_Display hex_digit_display_5 (.value(Output[15:12]));  // open: dp
  Hex_Digit_Display hex_digit_display_6 (.value(Output[11:8]));  // open: dp
  Hex_Digit_Display hex_digit_display_7 (.value(Output[7:4]));  // open: dp
  Hex_Digit_Display hex_digit_display_8 (.value(Output[3:0]));  // open: dp
  Multiplexer #(.select(4), .width(16), .enable("false")) multiplexer_1 (
    .in0({bit_extender_2_out, adder_1_out}), .in1({bit_extender_3_out, subtractor_1_out}),
    .in2({multiplier_1_cout, multiplier_1_out}), .in3({divider_1_rem, divider_1_out}),
    .in4(bit_extender_4_out), .in5(bit_extender_5_out), .in6(bit_extender_6_out), .in7(bit_extender_7_out),
    .in8(bit_extender_8_out), .in9(bit_extender_9_out), .in10(bit_extender_10_out),
    .in11(bit_extender_11_out), .in12({bit_extender_14_out, bit_extender_13_out, bit_extender_12_out}),
    .out(Output), .sel(Opcode));  // open: in13, in14, in15
endmodule
