// Logisim project SUBTRACTOR.circ as structural Verilog: 1 circuit, main circuit main
module main (
  input  in_1,
  input  in_2,
  input  in_3,
  input  in_4,
  input  in_5,
  output DIFFERENCE,
  output out_7,
  output out_8,
  output out_9
);

  wire and_2_out, and_3_out, not_1_out, not_2_out, not_3_out, xor_2_out;

  xor xor_1 (DIFFERENCE, in_1, in_2);
  not not_1 (not_1_out, in_1);
  not not_2 (not_2_out, in_4);
  and and_1 (out_7, not_1_out, in_2);
  xor xor_2 (xor_2_out, in_4, in_5);
  and and_2 (and_2_out, in_5, not_2_out);
  xor xor_3 (out_8, in_3, xor_2_out);
  not not_3 (not_3_out, xor_2_out);
  and and_3 (and_3_out, not_3_out, in_3);
  or or_1 (out_9, and_3_out, and_2_out);

  // Notes on the sheet:
  //   BORROW
endmodule
