// Logisim project all gates.circ as structural Verilog: 1 circuit, main circuit main
module main (
  input  A,
  input  B,
  input  A_2,
  input  A_3,
  input  B_2,
  input  A_4,
  input  A_5,
  input  B_3,
  input  A_6,
  input  B_4,
  input  in_11,
  input  in_12,
  output A_B,
  output minus_A,
  output A_B_2,
  output out_16,
  output _7_A_B,
  output out_18,
  output out_19
);

  and and_1 (A_B, A, B);
  not not_1 (minus_A, A_2);
  or or_1 (A_B_2, A_3, B_2);
  buf buffer_1 (out_16, A_4);
  nand nand_1 (_7_A_B, A_5, B_3);
  nor nor_1 (out_18, A_6, B_4);
  xor xor_1 (out_19, in_11, in_12);

  // Notes on the sheet:
  //   OR
  //   AND GATE
  //   NOT GATE
  //   BUFFER
  //   NAND GATE
endmodule
