// Logisim project alu.circ as structural Verilog: 3 circuits, main circuit main
module main (
  input  A,
  input  B,
  input  [2:0] in_3,
  output out_4
);

  wire adder_1_out, and_1_out, nand_1_out, or_1_out, subtractor_1_out, xor_1_out;

  Adder #(.width(1)) adder_1 (.a(A), .b(B), .out(adder_1_out));  // open: cin, cout
  Subtractor #(.width(1)) subtractor_1 (.a(A), .b(B), .out(subtractor_1_out));  // open: bin, bout
  or or_1 (or_1_out, A, B);
  and and_1 (and_1_out, A, B);
  nand nand_1 (nand_1_out, A, B);
  xor xor_1 (xor_1_out, A, B);
  Multiplexer #(.select(3)) multiplexer_1 (
    .in0(adder_1_out), .in1(subtractor_1_out), .in2(or_1_out), .in3(and_1_out), .in4(nand_1_out),
    .in7(xor_1_out), .out(out_4), .sel(in_3));  // open: in5, in6, en

  // Notes on the sheet:
  //   1 BIT ALU
endmodule

module _8BITALU (
  input  [7:0] A,
  input  [7:0] B,
  input  [2:0] in_3,
  output [7:0] out_4
);

  wire [7:0] adder_1_out, and_1_out, nand_1_out, or_1_out, subtractor_1_out, xor_1_out;

  Adder adder_1 (.a(A), .b(B), .out(adder_1_out));  // open: cin, cout
  Subtractor subtractor_1 (.a(A), .b(B), .out(subtractor_1_out));  // open: bin, bout
  assign or_1_out = A | B;  // OR_Gate or_1, 8 bits wide
  assign and_1_out = A & B;  // AND_Gate and_1, 8 bits wide
  assign nand_1_out = ~(A & B);  // NAND_Gate nand_1, 8 bits wide
  assign xor_1_out = A ^ B;  // XOR_Gate xor_1, 8 bits wide
  Multiplexer #(.select(3), .width(8)) multiplexer_1 (
    .in0(adder_1_out), .in1(subtractor_1_out), .in2(or_1_out), .in3(and_1_out), .in4(nand_1_out),
    .in7(xor_1_out), .out(out_4), .sel(in_3));  // open: in5, in6, en
endmodule

module DESIGNING_ALU (
  input  [7:0] in_1,
  input  [7:0] in_2,
  input  [15:0] in_3,
  input  [2:0] in_4,
  input  [2:0] in_5
);

  wire adder_1_cout, subtractor_1_bout;
  wire [2:0] undriven;
  wire [7:0] adder_1_out, and_1_out, bit_extender_1_out, bit_extender_2_out, divider_1_out, divider_1_rem,
       multiplier_1_cout, multiplier_1_out, or_1_out, shifter_1_out, shifter_2_out, subtractor_1_out;
  wire [15:0] bit_extender_3_out, bit_extender_4_out, bit_extender_5_out, bit_extender_6_out;

  Hex_Digit_Display hex_digit_display_1 (.value(in_1[7:4]));  // open: dp
  Hex_Digit_Display hex_digit_display_2 (.value(in_1[3:0]));  // open: dp
  Hex_Digit_Display hex_digit_display_3 (.value(in_2[3:0]));  // open: dp
  Hex_Digit_Display hex_digit_display_4 (.value(in_2[7:4]));  // open: dp
  Adder adder_1 (.a(in_1), .b(in_2), .out(adder_1_out), .cout(adder_1_cout));  // open: cin
  Subtractor subtractor_1 (.a(in_1), .b(in_2), .out(subtractor_1_out), .bout(subtractor_1_bout));  // open: bin
  Multiplier multiplier_1 (.a(in_1), .b(in_2), .out(multiplier_1_out), .cout(multiplier_1_cout));  // open: cin
  Divider divider_1 (.a(in_1), .b(in_2), .out(divider_1_out), .rem(divider_1_rem));  // open: upper
  Shifter #(.shift("rl")) shifter_1 (.in(in_2), .\dist (in_5), .out(shifter_1_out));
  Shifter #(.shift("rr")) shifter_2 (.in(in_2), .\dist (in_5), .out(shifter_2_out));
  assign and_1_out = in_1 & in_2;  // AND_Gate and_1, 8 bits wide
  assign or_1_out = in_1 | in_2;  // OR_Gate or_1, 8 bits wide
  assign bit_extender_1_out = {{7{1'b0}}, adder_1_cout};  // Bit_Extender bit_extender_1
  assign bit_extender_2_out = {{7{1'b0}}, subtractor_1_bout};  // Bit_Extender bit_extender_2
  assign bit_extender_3_out = {{8{1'b0}}, and_1_out};  // Bit_Extender bit_extender_3
  assign bit_extender_4_out = {{8{1'b0}}, or_1_out};  // Bit_Extender bit_extender_4
  assign bit_extender_5_out = {{8{1'b0}}, shifter_1_out};  // Bit_Extender bit_extender_5
  assign bit_extender_6_out = {{8{1'b0}}, shifter_2_out};  // Bit_Extender bit_extender_6
  Multiplexer #(.select(3), .width(16)) multiplexer_1 (
    .in0({bit_extender_1_out, adder_1_out}), .in1({bit_extender_2_out, subtractor_1_out}),
    .in2({multiplier_1_cout, multiplier_1_out}), .in3({divider_1_rem, divider_1_out}),
    .in4(bit_extender_3_out), .in5(bit_extender_4_out), .in6(bit_extender_5_out), .in7(bit_extender_6_out),
    .out(in_3), .sel(undriven));  // open: en
endmodule
