// Logisim project impl of boolen expr using basic gates.circ as structural Verilog: 1 circuit, main circuit main
module main (
  input  x,
  input  y,
  input  z,
  input  A,
  input  B,
  input  C,
  input  X_2,
  input  W,
  input  Y_2,
  input  Z_2,
  input  in_11,
  input  in_12,
  input  in_13,
  input  in_14,
  input  in_15,
  input  in_16,
  input  in_17,
  input  in_18,
  output out_19,
  output out_20,
  output out_21,
  output out_22,
  output out_23
);

  wire and_1_out, and_2_out, and_3_out, and_4_out, and_5_out, and_7_out, and_8_out, not_1_out, not_2_out,
       not_3_out, not_4_out, not_5_out, not_6_out, not_7_out, not_8_out, or_2_out, or_3_out;

  not not_1 (not_1_out, W);
  not not_2 (not_2_out, Y_2);
  not not_3 (not_3_out, Z_2);
  not not_4 (not_4_out, in_11);
  not not_5 (not_5_out, in_12);
  not not_6 (not_6_out, x);
  and and_1 (and_1_out, y, z);
  and and_2 (and_2_out, A, B);
  and and_3 (and_3_out, B, C);
  and and_4 (and_4_out, in_11, not_5_out);
  not not_7 (not_7_out, in_13);
  not not_8 (not_8_out, in_14);
  and and_5 (and_5_out, in_16, in_17);
  // AND_Gate and_6 is placed but not wired
  and and_7 (and_7_out, not_1_out, not_2_out, not_3_out);
  // OR_Gate or_1 has open pins: in1=and_5_out, in3=in_18, out=open
  or or_2 (or_2_out, not_7_out, not_8_out);
  or or_3 (or_3_out, not_8_out, in_15);
  or or_4 (out_19, not_6_out, and_1_out);
  or or_5 (out_20, and_2_out, and_3_out);
  or or_6 (out_21, X_2, and_7_out);
  and and_8 (and_8_out, in_12, not_4_out);
  and and_9 (out_23, or_2_out, or_3_out);
  or or_7 (out_22, and_4_out, and_8_out);

  // Notes on the sheet:
  //   7(x)
  //   yz
  //   AB
  //   BC
  //   7W.7Y.7Z
  //   7(X)+YZ
  //   AB+BC
  //   X+7W.7Y.7Z
endmodule
