// Logisim project impl_of_universal_gate_using_NAND.circ as structural Verilog: 1 circuit, main circuit main
module main (
  input  A,
  input  B,
  input  A_2,
  input  B_2,
  input  A_3,
  input  A_4,
  input  B_3,
  input  A_5,
  input  B_4,
  input  A_6,
  output A_B,
  output A_B_2,
  output _7_A,
  output out_14,
  output out_15,
  output _7_A_2
);

  wire nand_1_out, nand_2_out, nand_3_out, nor_1_out, nor_2_out, nor_3_out;

  nand nand_1 (nand_1_out, A, B);
  nand nand_2 (nand_2_out, A_2, A_2);
  nand nand_3 (nand_3_out, B_2, B_2);
  nor nor_1 (nor_1_out, A_5, B_4);
  nand nand_4 (_7_A, A_3, A_3);
  nor nor_2 (nor_2_out, A_4, A_4);
  nor nor_3 (nor_3_out, B_3, B_3);
  nor nor_4 (_7_A_2, A_6, A_6);
  nand nand_5 (A_B, nand_1_out, nand_1_out);
  nand nand_6 (A_B_2, nand_2_out, nand_3_out);
  nor nor_5 (out_15, nor_1_out, nor_1_out);
  nor nor_6 (out_14, nor_2_out, nor_3_out);

  // Notes on the sheet:
  //   IMPLEMENTATION OF UNIVERASAL GATE USING NAND
  //   IMPLEMENTATION OF BASIC GATES USING NOR
  //   AND GATE EQUIVALENT
  //   AND GATE EUIVALENT
  //   OR GATE EQUIVALENT
  //   OR GATE EQUIVALENT
  //   NOT GATE EQUIVALENT
  //   NOT GATE
endmodule
