// Logisim project registers.circ as structural Verilog: 1 circuit, main circuit main
module main (
  input  [7:0] in_1,
  input  [2:0] rx,
  input  r_w,
  output [7:0] out_4
);

  wire clock_1_out, decoder_1_out0, decoder_1_out1, decoder_1_out2, decoder_1_out3, decoder_1_out4,
       decoder_1_out5, decoder_1_out6, decoder_1_out7, not_1_out;
  wire [7:0] register_1_q, register_2_q, register_3_q, register_4_q, register_5_q, register_6_q,
       register_7_q, register_8_q;

  Clock clock_1 (.out(clock_1_out));
  not not_1 (not_1_out, r_w);
  Hex_Digit_Display hex_digit_display_1 (.value(in_1[7:4]));  // open: dp
  Hex_Digit_Display hex_digit_display_2 (.value(in_1[3:0]));  // open: dp
  Decoder #(.select(3), .disabled(0)) decoder_1 (
    .out0(decoder_1_out0), .out1(decoder_1_out1), .out2(decoder_1_out2), .out3(decoder_1_out3),
    .out4(decoder_1_out4), .out5(decoder_1_out5), .out6(decoder_1_out6), .out7(decoder_1_out7), .sel(rx),
    .en(not_1_out));
  Register register_1 (.D(in_1), .en(decoder_1_out0), .Q(register_1_q), .clk(clock_1_out));  // open: clr
  Register register_2 (.D(in_1), .en(decoder_1_out1), .Q(register_2_q), .clk(clock_1_out));  // open: clr
  Register register_3 (.D(in_1), .en(decoder_1_out2), .Q(register_3_q), .clk(clock_1_out));  // open: clr
  Register register_4 (.D(in_1), .en(decoder_1_out3), .Q(register_4_q), .clk(clock_1_out));  // open: clr
  Register register_5 (.D(in_1), .en(decoder_1_out4), .Q(register_5_q), .clk(clock_1_out));  // open: clr
  Register register_6 (.D(in_1), .en(decoder_1_out5), .Q(register_6_q), .clk(clock_1_out));  // open: clr
  Register register_7 (.D(in_1), .en(decoder_1_out6), .Q(register_7_q), .clk(clock_1_out));  // open: clr
  Register register_8 (.D(in_1), .en(decoder_1_out7), .Q(register_8_q), .clk(clock_1_out));  // open: clr
  Hex_Digit_Display hex_digit_display_3 (.value(out_4[3:0]));  // open: dp
  Hex_Digit_Display hex_digit_display_4 (.value(out_4[7:4]));  // open: dp
  Multiplexer #(.select(3), .width(8)) multiplexer_1 (
    .in0(register_1_q), .in1(register_2_q), .in2(register_3_q), .in3(register_4_q), .in4(register_5_q),
    .in5(register_6_q), .in6(register_7_q), .in7(register_8_q), .out(out_4), .sel(rx), .en(r_w));

  // Notes on the sheet:
  //   clock
  //   r=1
  //   w=0
  //   8-bit Register File(R0-R7)
  //   R1
  //   R2
  //   R3
  //   R4
  //   R5
  //   R6
  //   R7
  //   R8
endmodule
